# Fritzing sketch sensor clock 2 (saved by Fritzing 0.8.7b)
breadboards: 1

parts:
  DHT22 = Humidity and Temperature Sensor RHT03
  Part2 = Chronodot v2.1 DS3231
  R1 = Resistor [tolerance=±5% resistance=10k package=THT]
  Part3 = Arduino Uno (Rev3)
  LCD1 = LCD screen

nets:
  N1: DHT22.Vcc, R1.Pin_1
  N2: DHT22.Data-signal, R1.Pin_0, Part3.A0
  GND: DHT22.GND_2, Part2.GND, Part3.GND, LCD1.VSS
  5V: Part2.5V, Part3.5V, LCD1.VDD
  N3: Part2.SCL, Part3.A5/SCL, LCD1.V0
  N4: Part2.SDA, Part3.A4/SDA, LCD1.RS

custom parts:
  Chronodot v2.1 DS3231: Modified to DS3231 for naming purposes. This a custom designed module for the DS1307 Real Time Clock. The module comes fully assembled and pre-programmed with the current time (ok, so it's our current time - MST). The included Lithium coin cell battery (CR1225 41mAh) will run the module for a minimum of 9 years (17 years typical) without external 5V power. The DS1307 is accessed via the I2C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
